// Logisim project B22CS001.circ as structural Verilog: 5 circuits, main circuit main
module main (
  input  [3:0] ALU_Control,
  input  [31:0] in_2,
  input  [31:0] in_3,
  output out_4,
  output Branch,
  output [31:0] out_6
);

  wire adder_1_out_4, comparator_1_eq, comparator_1_lt, comparator_2_eq, comparator_3_eq, comparator_4_eq,
       multiplexer_5_out, not_1_out, subtractor_1_out_4;
  wire [31:0] adder_1_out_3, and_1_out, multiplexer_1_out, multiplexer_2_out, multiplexer_3_out, or_1_out,
       subtractor_1_out_3, xor_1_out;

  Adder adder_1 (.out_3(adder_1_out_3), .out_4(adder_1_out_4), .in_1(in_2), .in_2(in_3));
  Subtractor subtractor_1 (.out_3(subtractor_1_out_3), .out_4(subtractor_1_out_4), .in_1(in_2), .in_2(in_3));
  Comparator #(.width(32)) comparator_1 (.a(in_2), .b(in_3), .eq(comparator_1_eq), .lt(comparator_1_lt));  // open: gt
  not not_1 (not_1_out, comparator_1_eq);
  assign xor_1_out = in_2 ^ in_3;  // XOR_Gate xor_1, 32 bits wide
  assign or_1_out = in_2 | in_3;  // OR_Gate or_1, 32 bits wide
  assign and_1_out = in_2 & in_3;  // AND_Gate and_1, 32 bits wide
  Multiplexer #(.width(32), .enable("false")) multiplexer_1 (
    .in0({32{1'b0}}), .in1(32'h1), .out(multiplexer_1_out), .sel(comparator_1_lt));
  Multiplexer #(.width(32), .enable("false")) multiplexer_2 (
    .in0({32{1'b0}}), .in1(32'h1), .out(multiplexer_2_out), .sel(comparator_1_eq));
  Multiplexer #(.width(32), .enable("false")) multiplexer_3 (
    .in0({32{1'b0}}), .in1(32'h1), .out(multiplexer_3_out), .sel(not_1_out));
  Multiplexer #(.select(4), .width(32), .enable("false")) multiplexer_4 (
    .in0(adder_1_out_3), .in1(subtractor_1_out_3), .in2(multiplexer_1_out), .in3(xor_1_out), .in4(or_1_out),
    .in5(and_1_out), .in8(multiplexer_2_out), .in9(multiplexer_3_out), .out(out_6), .sel(ALU_Control));  // open: in6, in7, in10, in11, in12, in13, in14, in15
  Multiplexer #(.enable("false")) multiplexer_5 (
    .in0(adder_1_out_4), .in1(subtractor_1_out_4), .out(multiplexer_5_out), .sel(ALU_Control[0]));
  Comparator #(.width(3), .mode("unsigned")) comparator_2 (
    .a(ALU_Control[3:1]), .b(3'b000), .eq(comparator_2_eq));  // open: gt, lt
  Comparator #(.width(1), .mode("unsigned")) comparator_3 (
    .a(ALU_Control[3]), .b(1'b1), .eq(comparator_3_eq));  // open: gt, lt
  Comparator #(.width(32), .mode("unsigned")) comparator_4 (
    .a(32'h1), .b(out_6), .eq(comparator_4_eq));  // open: gt, lt
  and and_2 (out_4, comparator_2_eq, multiplexer_5_out);
  and and_3 (Branch, comparator_3_eq, comparator_4_eq);

  // Notes on the sheet:
  //   A
  //   B
  //   , ADDI
  //   ADD
  //   SUB
  //   , SUBI
  //   XOR
  //   , XORI
  //   OR
  //   , ORI
  //   , ANDI
  //   AND
  //   SLT
  //   BEQ
  //   BNE
  //   OVERFLOW
  //   UNDERFLOW
  //   Output
  //   OVERFLOW / UNDERFLOW
endmodule

module Adder (
  input  [31:0] in_1,
  input  [31:0] in_2,
  output [31:0] out_3,
  output out_4
);

  Adder_part #(.width(32)) adder_1 (.a(in_1), .b(in_2), .out(out_3));  // open: cin, cout
  Comparator #(.width(32)) comparator_1 (.a(in_1), .b(out_3), .lt(out_4));  // open: gt, eq

  // Notes on the sheet:
  //   ADDER__CKT
endmodule

module Subtractor (
  input  [31:0] in_1,
  input  [31:0] in_2,
  output [31:0] out_3,
  output out_4
);

  Subtractor_part #(.width(32)) subtractor_1 (.a(in_1), .b(in_2), .out(out_3));  // open: bin, bout
  Comparator #(.width(32)) comparator_1 (.a(out_3), .b(in_1), .lt(out_4));  // open: gt, eq
endmodule

module Control_Unit (
  input  [31:0] Binary_Instruction,
  output [5:0] Funct,
  output Jump,
  output ALURequired,
  output RegDest,
  output Branch,
  output MemWrite,
  output MemRead,
  output MemToReg,
  output RegWrite,
  output ALUSrc,
  output R_type,
  output [1:0] ALUOp
);

  wire ADDI_out, ANDI_out, BEQ_out, BNE_out, ORI_out, SLTI_out, XORI_out;

  and u_R_type (R_type, ~Binary_Instruction[31], ~Binary_Instruction[30], ~Binary_Instruction[29], ~Binary_Instruction[28], ~Binary_Instruction[27], ~Binary_Instruction[26]);  // AND_Gate
  and LW (MemRead, Binary_Instruction[31], ~Binary_Instruction[30], ~Binary_Instruction[29], ~Binary_Instruction[28], Binary_Instruction[27], Binary_Instruction[26]);  // AND_Gate
  and SW (MemWrite, Binary_Instruction[31], ~Binary_Instruction[30], Binary_Instruction[29], ~Binary_Instruction[28], Binary_Instruction[27], Binary_Instruction[26]);  // AND_Gate
  and BEQ (BEQ_out, ~Binary_Instruction[31], ~Binary_Instruction[30], ~Binary_Instruction[29], Binary_Instruction[28], ~Binary_Instruction[27], ~Binary_Instruction[26]);  // AND_Gate
  and ADDI (ADDI_out, ~Binary_Instruction[31], ~Binary_Instruction[30], Binary_Instruction[29], ~Binary_Instruction[28], ~Binary_Instruction[27], ~Binary_Instruction[26]);  // AND_Gate
  and SLTI (SLTI_out, ~Binary_Instruction[31], ~Binary_Instruction[30], Binary_Instruction[29], ~Binary_Instruction[28], Binary_Instruction[27], ~Binary_Instruction[26]);  // AND_Gate
  and ANDI (ANDI_out, ~Binary_Instruction[31], ~Binary_Instruction[30], Binary_Instruction[29], Binary_Instruction[28], ~Binary_Instruction[27], ~Binary_Instruction[26]);  // AND_Gate
  and ORI (ORI_out, ~Binary_Instruction[31], ~Binary_Instruction[30], Binary_Instruction[29], Binary_Instruction[28], ~Binary_Instruction[27], Binary_Instruction[26]);  // AND_Gate
  and XORI (XORI_out, ~Binary_Instruction[31], ~Binary_Instruction[30], Binary_Instruction[29], Binary_Instruction[28], Binary_Instruction[27], ~Binary_Instruction[26]);  // AND_Gate
  ROM #(.addrWidth(6), .dataWidth(2)) rom_1 (.addr(Binary_Instruction[31:26]), .data(ALUOp));  // open: sel
  and J (Jump, ~Binary_Instruction[31], ~Binary_Instruction[30], ~Binary_Instruction[29], ~Binary_Instruction[28], Binary_Instruction[27], ~Binary_Instruction[26]);  // AND_Gate
  and BNE (BNE_out, ~Binary_Instruction[31], ~Binary_Instruction[30], ~Binary_Instruction[29], Binary_Instruction[28], ~Binary_Instruction[27], Binary_Instruction[26]);  // AND_Gate
  not not_1 (ALURequired, Jump);
  or or_1 (Branch, BNE_out, BEQ_out);
  or u_RegWrite (RegWrite, XORI_out, ORI_out, ANDI_out, SLTI_out, ADDI_out, MemRead, R_type);
  nor nor_1 (ALUSrc, BNE_out, BEQ_out, R_type);

  assign Funct = Binary_Instruction[5:0];
  assign MemToReg = MemRead;
  assign RegDest = R_type;

  // Other names for the same wires on the sheet: Opcode[5:0] = Binary_Instruction[31:26]

  // Notes on the sheet:
  //   contents of rom_1 (hex, n*v repeats v):
  //   2 0 0 0 1 1 4*0 3 0 3 3 3
endmodule

module ALU_CTRL (
  input  [5:0] OPCODE,
  input  [5:0] Funct,
  input  R_type,
  output [3:0] ALU_CONTROL
);

  wire ADD_out, or_2_out;
  wire [3:0] multiplexer_1_out;
  wire [8:0] multiplexer_2_out;

  Multiplexer #(.width(4), .enable("false")) multiplexer_1 (
    .in0(4'b0001), .in1(Funct[3:0]), .out(multiplexer_1_out), .sel(R_type));
  Multiplexer #(.enable("false")) multiplexer_2 (.in0(ADD_out), .in1(1'b0), .out(multiplexer_2_out[0]), .sel(or_2_out));
  and ADD (ADD_out, ~multiplexer_1_out[3], ~multiplexer_1_out[2], ~multiplexer_1_out[1], ~multiplexer_1_out[0]);  // AND_Gate
  and SUB (multiplexer_2_out[1], ~multiplexer_1_out[3], ~multiplexer_1_out[2], multiplexer_1_out[1], ~multiplexer_1_out[0]);  // AND_Gate
  and AND (multiplexer_2_out[2], ~multiplexer_1_out[3], multiplexer_1_out[2], ~multiplexer_1_out[1], ~multiplexer_1_out[0]);  // AND_Gate
  ROM #(.addrWidth(9), .dataWidth(4)) rom_1 (.addr(multiplexer_2_out), .data(ALU_CONTROL));  // open: sel
  and XOR (multiplexer_2_out[4], ~multiplexer_1_out[3], multiplexer_1_out[2], multiplexer_1_out[1], ~multiplexer_1_out[0]);  // AND_Gate
  and OR (multiplexer_2_out[3], ~multiplexer_1_out[3], multiplexer_1_out[2], ~multiplexer_1_out[1], multiplexer_1_out[0]);  // AND_Gate
  and SLT (multiplexer_2_out[5], multiplexer_1_out[3], ~multiplexer_1_out[2], multiplexer_1_out[1], ~multiplexer_1_out[0]);  // AND_Gate
  or or_2 (or_2_out, multiplexer_2_out[6], multiplexer_2_out[7], multiplexer_2_out[8]);
  Comparator #(.width(6)) comparator_1 (.a(OPCODE), .b(6'b000100), .eq(multiplexer_2_out[6]));  // open: gt, lt
  Comparator #(.width(6)) comparator_2 (.a(OPCODE), .b(6'b000101), .eq(multiplexer_2_out[7]));  // open: gt, lt
  Comparator #(.width(6)) comparator_3 (.a(OPCODE), .b(6'b001000), .eq(multiplexer_2_out[8]));  // open: gt, lt

  // Notes on the sheet:
  //   contents of rom_1 (hex, n*v repeats v):
  //   0 0 1 0 5 0 0 0 4 7*0 3 15*0 2 31*0 8 63*0 9
  //   BEQ
  //   BNE
  //   ADDI
endmodule
